// Logisim project CPU.circ as structural Verilog: 7 circuits, main circuit Main
module Pin_check (
  input  [7:0] in_1,
  input  [15:0] in_2,
  input  in_3,
  input  in_4,
  input  in_5
);

  wire main_1_d0_2, main_1_d1_2, main_1_d2_2, main_1_d3_2, main_1_d4_2, main_1_d5_2, main_1_d6_2, main_1_d7_2;

  Main main_1 (
    .D4_2(main_1_d4_2), .D5_2(main_1_d5_2), .D6_2(main_1_d6_2), .D7_2(main_1_d7_2), .D3_2(main_1_d3_2),
    .D2_2(main_1_d2_2), .D1_2(main_1_d1_2), .D0_2(main_1_d0_2), .D4(main_1_d4_2), .D5(main_1_d5_2),
    .D6(main_1_d6_2), .D7(main_1_d7_2), .D3(main_1_d3_2), .D2(main_1_d2_2), .D1(main_1_d1_2), .D0(main_1_d0_2));  // open: A10, A11, A14, A13, A12, A15, A9, A8, A7, A6, A5, A4, A3, A2, A1, A0, Vss, Vcc, Vbb, Vdd, WR, DBIN, INTE, INT, HLDA, Hold, Wait, Ready, Sync, Phase1, Phase2, Reset, Read_Write_Mem, Read_Write_into_Register, Instr_Register_Write, Mux, Read, Write, Inc_Dec
  RAM #(.addrWidth(16)) ram_1 (.addr(in_2), .data(in_1), .sel(in_5), .clk(in_4), .ld(in_3));  // open: clr
endmodule

module Main (
  input  D7,
  input  D6,
  input  D5,
  input  D4,
  input  D3,
  input  D2,
  input  D1,
  input  D0,
  input  Inc_Dec,
  input  [3:0] Read,
  input  [3:0] Mux,
  input  [3:0] Write,
  input  Read_Write_Mem,
  input  Instr_Register_Write,
  input  Read_Write_into_Register,
  input  Vss,
  input  Vbb,
  input  Vcc,
  input  Vdd,
  input  INTE,
  input  Phase2,
  input  Hold,
  input  Ready,
  input  Phase1,
  input  Reset,
  output D7_2,
  output D6_2,
  output D5_2,
  output D4_2,
  output D3_2,
  output D2_2,
  output D1_2,
  output D0_2,
  output A15,
  output A14,
  output A13,
  output A12,
  output A11,
  output A10,
  output A9,
  output A8,
  output A7,
  output A6,
  output A5,
  output A4,
  output A3,
  output A2,
  output A1,
  output A0,
  output WR,
  output HLDA,
  output Wait,
  output Sync,
  output DBIN,
  output INT
);

  wire and_1_out, Clock, n3_8_decoder_1_y2, n3_8_decoder_1_y4, n3_8_decoder_1_y5, n3_8_decoder_1_y6;
  wire [0:0] timing_and_control_1_registry_control;
  wire [1:0] timing_and_control_1_en_right_2;
  wire [2:0] timing_and_control_1_en_left;
  wire [3:0] timing_and_control_1_alu_control, timing_and_control_1_registry_control_2,
       timing_and_control_1_registry_control_3, timing_and_control_1_registry_control_4;
  wire [6:0] timing_and_control_1_en_right;
  wire [7:0] alu_1_flag_out_e4e05d57, alu_1_result, controlled_buffer_1_out, controlled_buffer_2_out,
       controlled_buffer_3_out, controlled_buffer_6_out, E1, E2, E3, E4, E5, E6, scratch_pad_1_bus_out;
  wire [15:0] scratch_pad_1_mem_bus;

  assign controlled_buffer_1_out = n3_8_decoder_1_y4 ? controlled_buffer_3_out : 8'bz;  // Controlled_Buffer controlled_buffer_1
  CPU_Register cpu_register_1 (.Clk(Clock), .In(controlled_buffer_1_out), .Out(E1));  // open: En
  assign controlled_buffer_2_out = n3_8_decoder_1_y5 ? controlled_buffer_3_out : 8'bz;  // Controlled_Buffer controlled_buffer_2
  CPU_Register cpu_register_2 (.Clk(Clock), .In(controlled_buffer_2_out), .Out(E3));  // open: En
  Accumulator_Latch accumulator_latch_1 (.In(E1), .Out(E2));  // open: Clk
  CPU_Register cpu_register_3 (.Clk(Clock), .In(alu_1_flag_out_e4e05d57), .Out(E4));  // open: En
  ALU alu_1 (
    .Flag_in_cff6aa82(E4), .A(E2), .B(E3), .OpCode(timing_and_control_1_alu_control),
    .Flag_Out_e4e05d57(alu_1_flag_out_e4e05d57), .Result(alu_1_result));
  assign controlled_buffer_3_out = n3_8_decoder_1_y2 ? E4 : 8'bz;  // Controlled_Buffer controlled_buffer_3
  assign controlled_buffer_3_out = n3_8_decoder_1_y6 ? alu_1_result : 8'bz;  // Controlled_Buffer controlled_buffer_4
  _3_8_Decoder u_3_8_decoder_1 (
    .En(1'b1), .y2(n3_8_decoder_1_y2), .Select(timing_and_control_1_en_left), .y4(n3_8_decoder_1_y4),
    .y5(n3_8_decoder_1_y5), .y6(n3_8_decoder_1_y6));  // open: y0, y1, y3, y7
  and and_1 (and_1_out, ~Vss, ~Vbb, Vcc, Vdd);  // AND_Gate
  Dual_CPU_Buffer dual_cpu_buffer_1 (
    .Direction(timing_and_control_1_en_right[6]), .Out0(controlled_buffer_3_out),
    .Out1({D7, D6, D5, D4, D3, D2, D1, D0}), .In1(controlled_buffer_3_out),
    .In0({D7, D6, D5, D4, D3, D2, D1, D0}), .En(timing_and_control_1_en_right_2));
  Timing_and_Control timing_and_control_1 (
    .En_Left(timing_and_control_1_en_left),
    .En_Right({timing_and_control_1_en_right[6], timing_and_control_1_en_right_2, timing_and_control_1_en_right[3:0]}),
    .Clk(Clock),
    .Registry_Control({timing_and_control_1_registry_control_4, timing_and_control_1_registry_control_3, timing_and_control_1_registry_control_2, timing_and_control_1_registry_control[0]}),
    .ALU_Control(timing_and_control_1_alu_control), .En(and_1_out), .nWR(WR), .DBIN(DBIN), .INTE(INTE),
    .INTE_2(INT), .Hold_Ack(HLDA), .Hold(Hold), .Wait(Wait), .Ready(Ready), .Sync(Sync), .Ph1(Phase1),
    .Ph2(Phase2), .Reset(Reset), .Reg_Control_In({Mux, Read, Write, Inc_Dec}),
    .Read_Write_Memory(Read_Write_Mem), .Write_Instruction_Register(Instr_Register_Write),
    .Read_from_Register(Read_Write_into_Register));
  CPU_Register cpu_register_4 (
    .En(timing_and_control_1_en_right[2]), .Clk(Clock), .In(controlled_buffer_3_out), .Out(E5));
  Instruction_Decoder_and_Machine_Cycle_Encoding instruction_decoder_and_machine_cycle_encoding_1 (.Data_In(E5));  // open: Increment_Decrement, Bus_Read, Bus_Write
  // Probe on controlled_buffer_3_out
  assign controlled_buffer_3_out = timing_and_control_1_en_right[1] ? scratch_pad_1_bus_out : 8'bz;  // Controlled_Buffer controlled_buffer_5
  assign controlled_buffer_6_out = timing_and_control_1_en_right[1] ? controlled_buffer_3_out : 8'bz;  // Controlled_Buffer controlled_buffer_6
  Scratch_Pad scratch_pad_1 (
    .Bus_Read_Write(timing_and_control_1_registry_control_4), .Bus_Out(scratch_pad_1_bus_out),
    .Bus_In(controlled_buffer_6_out), .Clock(Clock),
    .Increment_Decrement(timing_and_control_1_registry_control[0]),
    .Write_Select(timing_and_control_1_registry_control_2), .Mem_Bus(scratch_pad_1_mem_bus),
    .Read_Select(timing_and_control_1_registry_control_3), .Error(E6));
  assign {A15, A14, A13, A12, A11, A10, A9, A8, A7, A6, A5, A4, A3, A2, A1, A0} = timing_and_control_1_en_right[0] ? scratch_pad_1_mem_bus : 16'bz;  // Controlled_Buffer controlled_buffer_7

  assign D0_2 = D0;
  assign D1_2 = D1;
  assign D2_2 = D2;
  assign D3_2 = D3;
  assign D4_2 = D4;
  assign D5_2 = D5;
  assign D6_2 = D6;
  assign D7_2 = D7;

  // Notes on the sheet:
  //   Reset: pull=down
  //   Any red lines here means Logisim has failed to load a register
endmodule

// Register
module CPU_Register (
  input  En,
  input  Clk,
  input  [7:0] In,
  output [7:0] Out
);

  Register__8 register_8_1 (.Clk(Clk), .In(In), .Out(Out), .W(En));  // open: Clear
endmodule

module Dual_CPU_Buffer (
  input  [1:0] En,
  input  [7:0] In0,
  input  [7:0] In1,
  input  Direction,
  output [7:0] Out0,
  output [7:0] Out1
);

  wire [7:0] latch_register_8_1_out, n2_1_demux_8_1__0, n2_1_demux_8_1__1, n2_1_mux_8_1_y;

  _2_1_Mux__8 u_2_1_mux_8_1 (._1(In1), ._0(In0), .Select(Direction), .Y(n2_1_mux_8_1_y));
  Latch_Register__8 latch_register_8_1 (.In(n2_1_mux_8_1_y), .Out(latch_register_8_1_out), .W(En[1]));  // open: Clear
  _2_1_Demux__8 u_2_1_demux_8_1 (
    ._1(n2_1_demux_8_1__1), ._0(n2_1_demux_8_1__0), .Select(Direction), .Y(latch_register_8_1_out));
  assign Out0 = En[0] ? n2_1_demux_8_1__0 : 8'bz;  // Controlled_Buffer controlled_buffer_1
  assign Out1 = En[0] ? n2_1_demux_8_1__1 : 8'bz;  // Controlled_Buffer controlled_buffer_2

  // Notes on the sheet:
  //   En: pull=down
  //   0 is from top
  //   1 is from bottom
endmodule

module Accumulator_Latch (
  input  [7:0] In,
  input  Clk,
  output [7:0] Out
);

  wire d_latch_1_p2, not_1_out, z_detector_1_1_out_2;

  Z_Detector__1 z_detector_1_1 (.out_2(z_detector_1_1_out_2), .in_1(In[7]));
  not not_1 (not_1_out, z_detector_1_1_out_2);
  // D_Latch d_latch_1: pin names not known; wires that end beside it: In[0], d_latch_1_p2, Out[0]
  // D_Latch d_latch_2: pin names not known; wires that end beside it: In[1], d_latch_1_p2, d_latch_1_p2, Out[1]
  // D_Latch d_latch_3: pin names not known; wires that end beside it: In[2], d_latch_1_p2, d_latch_1_p2, Out[2]
  // D_Latch d_latch_4: pin names not known; wires that end beside it: In[3], d_latch_1_p2, d_latch_1_p2, Out[3]
  // D_Latch d_latch_5: pin names not known; wires that end beside it: In[4], d_latch_1_p2, d_latch_1_p2, Out[4]
  // D_Latch d_latch_6: pin names not known; wires that end beside it: In[5], d_latch_1_p2, d_latch_1_p2, Out[5]
  // D_Latch d_latch_7: pin names not known; wires that end beside it: In[6], d_latch_1_p2, d_latch_1_p2, Out[6]
  D_Latch d_latch_8 (.Data(In[7]), .En(d_latch_1_p2), .Output(Out[7]));  // open: Clear
  and and_1 (d_latch_1_p2, not_1_out, Clk);

  // Notes on the sheet:
  //   Clk: pull=down
endmodule

module Timing_and_Control (
  input  Read_from_Register,
  input  Read_Write_Memory,
  input  Write_Instruction_Register,
  input  Reset,
  input  En,
  input  [12:0] Reg_Control_In,
  input  INTE,
  input  Ph2,
  input  Hold,
  input  Ready,
  input  Ph1,
  output [2:0] En_Left,
  output [6:0] En_Right,
  output Clk,
  output [3:0] ALU_Control,
  output [12:0] Registry_Control,
  output nWR,
  output Hold_Ack,
  output Wait,
  output Sync,
  output DBIN,
  output INTE_2
);

  Clock clock_1 (.out(Clk));

  assign ALU_Control = 4'b0000;
  assign DBIN = 1'b0;
  assign En_Left = 3'b000;
  assign {En_Right[6:4], En_Right[2:0]} = {{3{Read_Write_Memory}}, Write_Instruction_Register, Read_from_Register, Read_Write_Memory};
  assign Hold_Ack = 1'b0;
  assign INTE_2 = 1'b0;
  assign nWR = 1'b0;
  assign Registry_Control = Reg_Control_In;
  assign Sync = 1'b0;
  assign Wait = 1'b0;

  // Other names for the same wires on the sheet: Read_Write_Bus[3:0] = Reg_Control_In[3:0];
  //   Read[3:0] = Reg_Control_In[7:4]; Write[3:0] = Reg_Control_In[11:8]; Increment_decrement = Reg_Control_In[12]

  // Notes on the sheet:
  //   Write_Instruction_Register: pull=down
  //   Read_from_Register: pull=down
  //   En: pull=down
  //   En_Left: pull=down
  //   Read_Write_Memory: pull=down
  //   En_Right: pull=down
  //   4 Enable latch read
  //   5 Enable latch write
  //   6 Direction of Bus Latch
  //   0 Memory Bus 1: Register Buffer
  //   2 Instruction Register
endmodule

module Instruction_Decoder_and_Machine_Cycle_Encoding (
  input  [7:0] Data_In,
  output Bus_Read,
  output Bus_Write,
  output [3:0] Increment_Decrement
);

  wire [4:0] instruction_encoder_1_encoded_instruction_group;

  Instruction_Encoder instruction_encoder_1 (
    .Data_In(8'hc4), .Encoded_Instruction_Group(instruction_encoder_1_encoded_instruction_group));  // open: V
  // Probe on instruction_encoder_1_encoded_instruction_group
endmodule
